# Fritzing sketch ads1299_gnd_mini (saved by Fritzing 0.7.12b)
breadboards: 1

parts:
  Teensy3_0(Above) = Teensy3.0 [package="DIP (Dual Inline) [THT]"]
  J3(Below) = double row male pin header, 20 pins [form="♂ (male)"]
  Bluetooth = female pin header, 4 pins [form="♀ (female)"]
  LP2954(Above) = Voltage Regulator - 5V [package="TO220 [THT]"]
  Battery = female pin header, 2 pins [form="♀ (female)"]
  4_7uF = Electrolytic Capacitor [capacitance=1µF package="100 mil [THT, electrolytic]"]
  C104 = Ceramic Capacitor [capacitance=100nF package="100 mil [THT, multilayer]"]
  PowerSwitch = female pin header, 2 pins [form="♀ (female)"]
  0_ohm_1/10w = Resistor [tolerance=±5% resistance=220 package=THT]
  J2_Dummy(Below) = double row male pin header, 20 pins [form="♂ (male)"]  # not connected
  J4(Below) = double row male pin header, 10 pins [form="♂ (male)"]
  Optional = female pin header, 6 pins [form="♀ (female)"]
  LED = LED - 3mm [color="Red (633nm)" package="3 mm [THT]"]
  470 = Resistor [tolerance=±5% resistance=220 package=THT]
  4_7uF1 = Electrolytic Capacitor [capacitance=1µF package="100 mil [THT, electrolytic]"]

nets:
  N1: Teensy3_0(Above).pin1, Teensy3_0(Above).pin27, Bluetooth.pin2, LP2954(Above).GND, Battery.pin1, 4_7uF.-, C104.0, 0_ohm_1/10w.Pin_1, J4(Below).pin8, Optional.pin5, LED.cathode, 4_7uF1.-
  N2: Teensy3_0(Above).pin2, Bluetooth.pin3
  N3: Teensy3_0(Above).pin3, Bluetooth.pin4
  N4: Teensy3_0(Above).pin6, J3(Below).pin7
  N5: Teensy3_0(Above).pin7, J3(Below).pin13
  N6: Teensy3_0(Above).pin12, J3(Below).pin20
  N7: Teensy3_0(Above).pin13, J3(Below).pin15
  N8: Teensy3_0(Above).pin14, J3(Below).pin14
  N9: Teensy3_0(Above).pin15, J3(Below).pin19
  N10: Teensy3_0(Above).pin18, Optional.pin1
  N11: Teensy3_0(Above).pin19, Optional.pin2
  N12: Teensy3_0(Above).pin20, Optional.pin3
  N13: Teensy3_0(Above).pin21, Optional.pin4
  N14: Teensy3_0(Above).pin26, J4(Below).pin6, Optional.pin6
  N15: Teensy3_0(Above).pin28, Bluetooth.pin1, LP2954(Above).output_voltage, 4_7uF.+, C104.1, J4(Below).pin5, 470.Pin_1
  N16: J3(Below).pin2, 0_ohm_1/10w.Pin_0
  N17: LP2954(Above).input_voltage, PowerSwitch.pin1, 4_7uF1.+
  N18: Battery.pin2, PowerSwitch.pin2
  N19: LED.anode, 470.Pin_0

notes:
  SCLK
  CS
  DIN
  DOUT
  DRDY
  START
  3
  2
  1_TX
  0_RX
  Gnd
  Vcc
  3v3
  12_DIN
  11_DOUT
  10_CS
  9
  4_START
  5_DRDY
  6
  7
  8
  TXD
  RXD
  >5v
  AGND
  ads1299_demo
  13_SCLK
  AREF
  16_A2
  17_A3
  18_A4
  19_A5
  A5
  A4
  A2
  A3
  fuse

custom parts:
  Teensy3.0: A DIP stand-in part for whatever IC you want. With 28 pins on a 600mil dual inline package (DIP) footprint.
